// Logisim project A.1.circ as structural Verilog
module Ex1 (
  input  [7:0] input1,
  output out1,
  output [7:0] out2
);

  not not_1 (out2[7], input1[7]);
  and and_1 (out1, input1[0], input1[7]);

  assign out2[6:0] = input1[6:0];
endmodule
