// Logisim project alu.circ as structural Verilog: 3 circuits, main circuit main
// Mulad function is 30 in MUX
module main (
  input  [31:0] X,
  input  [31:0] Y,
  input  clock,
  input  Mul_Div_Reset,
  input  [5:0] Switch__S,
  output Signed_Overflow,
  output [31:0] RESULT,
  output Equal
);

  wire add_funct, add_overflow, comparator_3_eq, comparator_6_eq, comparator_7_lt, comparator_8_lt,
       comparator_9_eq, multiplexer_3_out, multiplexer_4_out, not_1_out, not_2_out, not_3_out, same_top_bit,
       sub_funct, sub_overflow;
  wire [4:0] bit_extender_1_out, bit_extender_2_out, bit_extender_4_out;
  wire [15:0] reverse_bit_1_out;
  wire [31:0] add, addu, \and , bitpal, \or , sll, slt, sltu, sra, srl, sub, subu;
  wire [31:16] lfsr;

  Bit_Extender #(.in_width(32), .out_width(5)) bit_extender_1 (.in(Y), .out(bit_extender_1_out));
  Comparator #(.width(5)) comparator_1 (
    .a({Switch__S[5], Switch__S[3:0]}), .b(5'b10000), .eq(add_funct));  // open: gt, lt
  Comparator #(.width(5)) comparator_2 (
    .a({Switch__S[5], Switch__S[3:0]}), .b(5'b10010), .eq(sub_funct));  // open: gt, lt
  Subtractor #(.width(32)) subtractor_1 (.a(X), .b(Y), .out(subu));  // open: bin, bout
  assign \and  = X & Y;  // AND_Gate and_1, 32 bits wide
  Shifter #(.width(32)) shifter_1 (.in(X), .\dist (bit_extender_1_out), .out(sll));
  Adder #(.width(32)) adder_1 (.a(X), .b(Y), .out(add));  // open: cin, cout
  Comparator #(.width(1)) comparator_3 (.a(X[31]), .b(add[31]), .eq(comparator_3_eq));  // open: gt, lt
  not not_1 (not_1_out, comparator_3_eq);
  reverse_bit reverse_bit_1 (.in_1(X[15:0]), .out(reverse_bit_1_out));
  Bit_Extender #(.in_width(32), .out_width(5)) bit_extender_2 (.in(Y), .out(bit_extender_2_out));
  Comparator #(.width(32)) comparator_4 (.a(X), .b(Y), .eq(Equal));  // open: gt, lt
  Multiplexer multiplexer_1 (.in0(1'b0), .in1(not_1_out), .out(add_overflow), .sel(same_top_bit));  // open: en
  Comparator #(.width(1)) comparator_5 (.a(X[31]), .b(Y[31]), .eq(same_top_bit));  // open: gt, lt
  Comparator #(.width(16)) comparator_6 (.a(reverse_bit_1_out), .b(X[31:16]), .eq(comparator_6_eq));  // open: gt, lt
  Multiplexer #(.select(5), .width(32)) multiplexer_2 (
    .in0(sll), .in2(srl), .in3(sra), .in16(add), .in17(addu), .in18(sub), .in19(subu), .in20(\and ),
    .in21(\or ), .in26(slt), .in27(sltu), .in30(bitpal), .in31({lfsr, X[15:0]}), .out(RESULT),
    .sel({Switch__S[5], Switch__S[3:0]}));  // open: in1, in4, in5, in6, in7, in8, in9, in10, in11, in12, in13, in14, in15, in22, in23, in24, in25, in28, in29, en
  Adder #(.width(32)) adder_2 (.a(X), .b(Y), .out(addu));  // open: cin, cout
  assign \or  = X | Y;  // OR_Gate or_1, 32 bits wide
  Shifter #(.width(32), .shift("lr")) shifter_2 (.in(X), .\dist (bit_extender_2_out), .out(srl));
  lfsr lfsr_1 (.in_1(X[31:16]), .out(lfsr));
  assign bitpal = {{31{1'b0}}, comparator_6_eq};  // Bit_Extender bit_extender_3
  Multiplexer multiplexer_3 (.in0(sub_overflow), .in1(1'b0), .out(multiplexer_3_out), .sel(sub_funct));  // open: en
  Multiplexer multiplexer_4 (.in0(1'b0), .in1(add_overflow), .out(multiplexer_4_out), .sel(add_funct));  // open: en
  Comparator #(.width(32)) comparator_7 (.a(X), .b(Y), .lt(comparator_7_lt));  // open: gt, eq
  Comparator #(.width(32)) comparator_8 (.a(X), .b(Y), .lt(comparator_8_lt));  // open: gt, eq
  Bit_Extender #(.in_width(32), .out_width(5)) bit_extender_4 (.in(Y), .out(bit_extender_4_out));
  Subtractor #(.width(32)) subtractor_2 (.a(X), .b(Y), .out(sub));  // open: bin, bout
  Comparator #(.width(1)) comparator_9 (.a(X[31]), .b(sub[31]), .eq(comparator_9_eq));  // open: gt, lt
  or or_2 (Signed_Overflow, multiplexer_3_out, multiplexer_4_out);
  assign sltu = {{31{1'b0}}, comparator_7_lt};  // Bit_Extender bit_extender_5
  assign sltu = {{31{1'b0}}, comparator_8_lt};  // Bit_Extender bit_extender_6
  Shifter #(.width(32), .shift("ar")) shifter_3 (.in(X), .\dist (bit_extender_4_out), .out(sra));
  not not_2 (not_2_out, comparator_9_eq);
  not not_3 (not_3_out, same_top_bit);
  Multiplexer multiplexer_5 (.in0(1'b0), .in1(not_2_out), .out(sub_overflow), .sel(not_3_out));  // open: en

  // Other names for the same wires on the sheet: add_topbit = add[31]; clk = clock; iff_equal = Equal;
  //   lfsr[15:0] = X[15:0]; x_input[31:0] = X; reset = Mul_Div_Reset; sub_topbit = sub[31];
  //   switch[4:0] = {Switch__S[5], Switch__S[3:0]}; y_input[31:0] = Y

  // Notes on the sheet:
  //   INPUTS to your circuit
  //   INPUT to your circuit
  //   Add Function is 16 in MUX
  //   SUBU (Subtraction Unsigned)
  //   AND (Boolean &)
  //   SLL (Shift Left Logical)
  //   ADD (Addition)
  //   # Signed overflow if top bit is incorrectly found
  //   # If top two bits are not same, then will not overflow (sum -> 0)
  //   # If top two bits are same, different top bit for func -> overflow 
  //   Core ALU (MIPS) Functions
  //   IFF Equal Test
  //   Bitpal
  //   Reverse Bit 16-31
  //   DON'T CHANGE THE INPUTS AND OUTPUTS! IF YOU DO SO, YOU NEED TO MAKE SURE THE PINS ARE IN THE RIGHT PLACES!
  //   ADDU (Addition Unsigned)
  //   OR (Boolean |)
  //   SRL (Shift Right Logical)
  //   LFSR
  //   Overflow Detection
  //   # Use splitter (from lab 6) to grab only most significant (top) bit
  //   SLT (Set Less Than)
  //   SLTU (Set Less Than Unsigned)
  //   SRA (Shift Right Arithmatic)
  //   SUB (Subtraction)
  //   # Signed overflow if top bit is incorrectly found
  //   # If top two bits same, then will not overflow (diff -> 0)
  //   # If top two bits are not same, different top bit for func -> overflow 
  //   OUTPUTS of your circuit
endmodule

module reverse_bit (
  input  [15:0] in_1,
  output [15:0] out
);


  assign out = {in_1[0], in_1[1], in_1[2], in_1[3], in_1[4], in_1[5], in_1[6], in_1[7], in_1[8], in_1[9], in_1[10], in_1[11], in_1[12], in_1[13], in_1[14], in_1[15]};
endmodule

module lfsr (
  input  [15:0] in_1,
  output [15:0] out
);

  wire xor_1_out, xor_2_out, xor_3_out;
  wire [15:0] bit_extender_1_out, shifter_1_out, shifter_2_out;

  Shifter #(.width(16), .shift("lr")) shifter_1 (.in(in_1), .\dist (4'b0001), .out(shifter_1_out));
  xor xor_1 (xor_1_out, in_1[2], in_1[0]);
  xor xor_2 (xor_2_out, in_1[3], xor_1_out);
  xor xor_3 (xor_3_out, in_1[5], xor_2_out);
  assign bit_extender_1_out = {{15{1'b0}}, xor_3_out};  // Bit_Extender bit_extender_1
  Shifter #(.width(16)) shifter_2 (.in(bit_extender_1_out), .\dist (4'b1111), .out(shifter_2_out));
  assign out = shifter_1_out | shifter_2_out;  // OR_Gate or_1, 16 bits wide
endmodule
