// Logisim project cpu.circ as structural Verilog: 1 circuit, main circuit main
// b_eq
module main (
  input  [31:0] RS_READ_VALUE,
  input  [31:0] RT_READ_VALUE,
  input  [31:0] INSTRUCTION,
  input  CLOCK,
  input  RESET,
  output [31:0] t0,
  output [31:0] t1,
  output [31:0] t2,
  output [31:0] t3,
  output [4:0] RS,
  output [4:0] RT,
  output [4:0] Write_Register,
  output [31:0] RD_WRITE_VALUE,
  output RD_WRITE_ENABLE,
  output [23:0] FETCH_ADDRESS
);

  wire alu_src, and_1_out, and_2_out, and_3_out, and_4_out, and_5_out, b_eq, b_not_eq, b_taken,
       comparator_1_eq, comparator_2_lt, comparator_3_lt, comparator_4_lt, comparator_5_lt, comparator_6_lt,
       comparator_7_lt, j___link, j_reg, j_taken, j_type, l_upp_imm, nop_case, not_1_out, r_type, shift_type,
       undriven, using_temp, zero_ext;
  wire [1:0] multiplexer_1_out;
  wire [4:0] reg_written_to;
  wire [5:0] funct;
  wire [15:6] immediate;
  wire [23:0] adder_1_out, adder_2_out, adder_3_out, bit_extender_1_out, j_reg_pc, j_type_addr, jump_case_pc,
       multiplexer_2_out, multiplexer_3_out, multiplexer_10_out, nxt_prog_count;
  wire [31:0] bit_extender_2_out, bit_extender_3_out, bit_extender_4_out, bit_extender_5_out, cpu_return,
       extd_imm, multiplexer_4_out, multiplexer_8_out, multiplexer_11_out, multiplexer_12_out,
       multiplexer_16_out, multiplexer_17_out, read_data1, read_data2, rs_prop_reg, rt_prop_reg;
  wire [31:26] INSTRUCTION_t;

  Comparator #(.width(32)) comparator_1 (.a(rs_prop_reg), .b(rt_prop_reg), .eq(comparator_1_eq));  // open: gt, lt
  Adder #(.width(24)) adder_1 (.a(FETCH_ADDRESS), .b(24'h1), .out(adder_1_out));  // open: cin, cout
  Multiplexer #(.width(2)) multiplexer_1 (
    .in0(RT[1:0]), .in1(immediate[12:11]), .out(multiplexer_1_out), .sel(r_type));  // open: en
  Comparator #(.width(5)) comparator_2 (.a(5'b00111), .b(RS), .lt(comparator_2_lt));  // open: gt, eq
  Comparator #(.width(5)) comparator_3 (.a(RS), .b(5'b01100), .lt(comparator_3_lt));  // open: gt, eq
  Comparator #(.width(5)) comparator_4 (.a(5'b00111), .b(RT), .lt(comparator_4_lt));  // open: gt, eq
  Comparator #(.width(5)) comparator_5 (.a(RT), .b(5'b01100), .lt(comparator_5_lt));  // open: gt, eq
  Multiplexer #(.width(24)) multiplexer_2 (
    .in0(adder_1_out), .in1(FETCH_ADDRESS), .out(multiplexer_2_out), .sel(nop_case));  // open: en
  assign bit_extender_1_out = {{8{1'b0}}, {immediate, funct}};  // Bit_Extender bit_extender_1
  and and_1 (and_1_out, b_not_eq, not_1_out);
  not not_1 (not_1_out, comparator_1_eq);
  and and_2 (and_2_out, comparator_1_eq, b_eq);
  Adder #(.width(24)) adder_2 (.a(multiplexer_2_out), .b(bit_extender_1_out), .out(adder_2_out));  // open: cin, cout
  regfile_main main_1 (
    .Read_register_1(RS[1:0]), .Read_register_2(RT[1:0]), .write_register(multiplexer_1_out),
    .write_data(cpu_return), .t0_Value(t0), .t1_Value(t1), .t2_Value(t2), .t3_Value(t3),
    .RegWrite(and_3_out), .clock(CLOCK), .Read_Data_1(read_data1), .Read_Data_2(read_data2));
  and and_3 (and_3_out, RD_WRITE_ENABLE, using_temp);
  and and_4 (and_4_out, comparator_2_lt, comparator_3_lt);
  and and_5 (and_5_out, comparator_4_lt, comparator_5_lt);
  assign bit_extender_2_out = {{16{1'b0}}, {immediate, funct}};  // Bit_Extender bit_extender_2
  assign bit_extender_3_out = {{16{immediate[15]}}, {immediate, funct}};  // Bit_Extender bit_extender_3
  or or_1 (b_taken, and_1_out, and_2_out);
  Multiplexer #(.width(24)) multiplexer_3 (
    .in0(multiplexer_2_out), .in1(adder_2_out), .out(multiplexer_3_out), .sel(b_taken));  // open: en
  Multiplexer #(.width(32)) multiplexer_4 (
    .in0(INSTRUCTION), .in1({32{1'b0}}), .out(multiplexer_4_out), .sel(nop_case));  // open: en
  Multiplexer #(.width(32)) multiplexer_5 (
    .in0(RS_READ_VALUE), .in1(read_data1), .out(rt_prop_reg), .sel(and_4_out));  // open: en
  Multiplexer #(.width(32)) multiplexer_6 (
    .in0(RT_READ_VALUE), .in1(read_data2), .out(rt_prop_reg), .sel(and_5_out));  // open: en
  Multiplexer #(.width(32)) multiplexer_7 (
    .in0(bit_extender_2_out), .in1(bit_extender_3_out), .out(extd_imm), .sel(zero_ext));  // open: en
  Register #(.width(32)) register_1 (
    .D(multiplexer_4_out), .Q({INSTRUCTION_t, RS, RT, immediate, funct}), .clk(CLOCK));  // open: en, clr
  Multiplexer #(.width(32)) multiplexer_8 (
    .in0(rt_prop_reg), .in1(extd_imm), .out(multiplexer_8_out), .sel(alu_src));  // open: en
  Multiplexer #(.width(5)) multiplexer_9 (
    .in0(immediate[15:11]), .in1(RT), .out(reg_written_to), .sel(r_type));  // open: en
  Adder #(.width(24)) adder_3 (.a(FETCH_ADDRESS), .b(24'h100000), .out(adder_3_out));  // open: cin, cout
  Register #(.width(24)) register_2 (.D(nxt_prog_count), .Q(FETCH_ADDRESS), .clk(CLOCK));  // open: en, clr
  Multiplexer #(.width(24)) multiplexer_10 (
    .in0(multiplexer_3_out), .in1(jump_case_pc), .out(multiplexer_10_out), .sel(j_type));  // open: en
  Multiplexer #(.width(32)) multiplexer_11 (
    .in0(rt_prop_reg), .in1(multiplexer_8_out), .out(multiplexer_11_out), .sel(l_upp_imm));  // open: en
  assign bit_extender_4_out = {{8{1'b0}}, adder_3_out};  // Bit_Extender bit_extender_4
  Comparator #(.width(5)) comparator_6 (.a(5'b00111), .b(reg_written_to), .lt(comparator_6_lt));  // open: gt, eq
  Comparator #(.width(5)) comparator_7 (.a(reg_written_to), .b(5'b01100), .lt(comparator_7_lt));  // open: gt, eq
  Multiplexer #(.width(32)) multiplexer_12 (
    .in0(multiplexer_8_out), .in1(32'h10), .out(multiplexer_12_out), .sel(l_upp_imm));  // open: en
  assign bit_extender_5_out = {{27{1'b0}}, immediate[10:6]};  // Bit_Extender bit_extender_5
  Multiplexer #(.width(5)) multiplexer_13 (
    .in0(reg_written_to), .in1({5{1'b1}}), .out(Write_Register), .sel(j___link));  // open: en
  Multiplexer #(.width(32)) multiplexer_14 (
    .in0(cpu_return), .in1(bit_extender_4_out), .out(RD_WRITE_VALUE), .sel(j___link));  // open: en
  or or_2 (nop_case, j_taken, b_taken);
  Subtractor #(.width(24)) subtractor_1 (.a(j_type_addr), .b(24'h100000), .out(jump_case_pc));  // open: bin, bout
  Subtractor #(.width(24)) subtractor_2 (.a(rs_prop_reg[23:0]), .b(24'h100000), .out(j_reg_pc));  // open: bin, bout
  Multiplexer #(.width(24)) multiplexer_15 (
    .in0(multiplexer_10_out), .in1(j_reg_pc), .out(nxt_prog_count), .sel(j_reg));  // open: en
  Multiplexer #(.width(32)) multiplexer_16 (
    .in0(multiplexer_11_out), .in1(rt_prop_reg), .out(multiplexer_16_out), .sel(shift_type));  // open: en
  Multiplexer #(.width(32)) multiplexer_17 (
    .in0(multiplexer_12_out), .in1(bit_extender_5_out), .out(multiplexer_17_out), .sel(shift_type));  // open: en
  and and_6 (using_temp, comparator_6_lt, comparator_7_lt);
  LED led_1 (.in(undriven));
  // mem_main MEM: pin names not known

  // Other names for the same wires on the sheet: clk = CLOCK; immediate[5:0] = funct;
  //   INSTRUCTION_t[25:0] = {RS, RT, immediate, funct}; shanmt[4:0] = immediate[10:6]; rd_reg[4:0] = immediate[15:11];
  //   rt_reg[4:0] = RT; rs_reg[4:0] = RS; opcode[5:0] = INSTRUCTION_t; fetch_addr[23:0] = FETCH_ADDRESS;
  //   prog_count[23:0] = FETCH_ADDRESS; RS_VAL[31:0] = RS_READ_VALUE; rst = RESET; RT_VAL[31:0] = RT_READ_VALUE;
  //   write_enable = RD_WRITE_ENABLE; write_reg[4:0] = Write_Register; write_value[31:0] = RD_WRITE_VALUE

  // Notes on the sheet:
  //   # Only need 2 bits (mux chooses t regs)
  //   Framework
  //   1) Determine branch value to set next PC value
  //   # Increment PC if not branch (not nop)
  //   # If branch taken, add imm addr to PC (extend - MIPS sheet)
  //   B) Calculate the actual branch value for the next PC
  //   # To account for Regfile's 4 registers ($t0 - $t3)
  //   # Check if rs and rt are temps, use appropriate values
  //   These are outputs/inputs from run.circ
  //   # Call to lui causes 16 bit shift (Also uses only $rt values)
  //   # Set PC value on next clock cycle
  //   # Use nop for J or I type
  //   PC Value Adjustments
  //   # Use branch value unless jump case
  //   III) Use Regfile inputs and determine ALU inputs
  //   # ALUSrc determines immediate or register to be used
  //   # Account for shift details (uses stardard rt val)
  //   split the instruction
  //   # Only jal will write to the $ra regt.
  //   # Jal sets $ra to the next instruction after PC
  //   These are outputs to run.circ
  //   # Adjust for base addr (Remember: byte-addressed)
  //   Use rs reg (to store address) for JR funct
  //   # If reg is $t0 - $t3
  //   2) Find the next PC value based on instrcts called
endmodule
