// Logisim project regfile.circ as structural Verilog: 1 circuit, main circuit main
module main (
  input  [1:0] Read_register_1,
  input  [1:0] Read_register_2,
  input  [1:0] write_register,
  input  [31:0] write_data,
  input  RegWrite,
  input  clock,
  output [31:0] t0_Value,
  output [31:0] t1_Value,
  output [31:0] t2_Value,
  output [31:0] t3_Value,
  output [31:0] Read_Data_1,
  output [31:0] Read_Data_2
);

  Multiplexer #(.select(2), .width(32), .enable("false")) multiplexer_1 (
    .out(Read_Data_1), .sel(Read_register_1));  // open: in0, in1, in2, in3
  Multiplexer #(.select(2), .width(32), .enable("false")) multiplexer_2 (
    .out(Read_Data_2), .sel(Read_register_2));  // open: in0, in1, in2, in3

  // Notes on the sheet:
  //   These are INPUTS to the circuit
  //   These are INPUTS to the circuit
  //   DO NOT CHANGE THE LOCATIONS OF THE INPUTS/OUTPUTS! IF YOU DO SO, YOU NEED TO MAKE SURE THE PINS ARE AT THE RIGHT PLACE!
  //   These are OUTPUTS to the circuit
  //   Yet again, the clock is not an actual clock, but an input, one that will be driven from a higher circuit
  //   These are OUTPUTS to the circuit
endmodule
